# Fritzing sketch system_design (saved by Fritzing 1.0.7)
breadboards: 1

parts:
  Rasberry_Pi_Pico_W = Raspberry Pi Pico W
  HC-SR04_Sensor_1 = HC-SR04 Ultrasonic Distance Sensor
  HC-SR04_Sensor_2 = HC-SR04 Ultrasonic Distance Sensor
  HC-SR04_Sensor_3 = HC-SR04 Ultrasonic Distance Sensor
  HC-SR04_Sensor_4 = HC-SR04 Ultrasonic Distance Sensor
  DC_Mot_Enc1 = DC Motor with two-phase hall-encoder [part_number=VT-E-G25A-06-177E]
  DC_Mot_Enc2 = DC Motor with two-phase hall-encoder [part_number=VT-E-G25A-06-177E]
  Bat1 = battery_holder_single_18650
  Bat2 = battery_holder_single_18650
  Bat3 = battery_holder_single_18650
  Cytron_MDD10A = MDD10A
  Mod1 = Raspberry Pi 4B
  Part1 = Adafruit BNO085 9-DOF Orientation IMU Fusion [part_number="Addfruit #4754"]

nets:
  N1: Rasberry_Pi_Pico_W.pin_1, Cytron_MDD10A.no_name_yet#connectordir-1
  GND: Rasberry_Pi_Pico_W.pin_3, Rasberry_Pi_Pico_W.pin_8, Rasberry_Pi_Pico_W.pin_13, Rasberry_Pi_Pico_W.pin_18, Rasberry_Pi_Pico_W.pin_23, Rasberry_Pi_Pico_W.pin_28, Rasberry_Pi_Pico_W.pin_33, Rasberry_Pi_Pico_W.pin_38, Rasberry_Pi_Pico_W.pin_42, HC-SR04_Sensor_1.GND, HC-SR04_Sensor_2.GND, HC-SR04_Sensor_3.GND, HC-SR04_Sensor_4.GND, DC_Mot_Enc1.pin2, DC_Mot_Enc2.pin2, Cytron_MDD10A.no_name_yet#connectorgnd-1
  N2: Rasberry_Pi_Pico_W.pin_4, Cytron_MDD10A.no_name_yet#connectordir-2
  N3: Rasberry_Pi_Pico_W.pin_9, HC-SR04_Sensor_2.TRIG
  N4: Rasberry_Pi_Pico_W.pin_10, HC-SR04_Sensor_2.ECHO
  N5: Rasberry_Pi_Pico_W.pin_11, Cytron_MDD10A.no_name_yet#connectorpwm-1
  N6: Rasberry_Pi_Pico_W.pin_12, Cytron_MDD10A.no_name_yet#connectorpwm-2
  N7: Rasberry_Pi_Pico_W.pin_14, HC-SR04_Sensor_1.TRIG
  N8: Rasberry_Pi_Pico_W.pin_15, HC-SR04_Sensor_1.ECHO
  N9: Rasberry_Pi_Pico_W.pin_16, HC-SR04_Sensor_3.TRIG
  N10: Rasberry_Pi_Pico_W.pin_17, HC-SR04_Sensor_3.ECHO
  N11: Rasberry_Pi_Pico_W.pin_19, HC-SR04_Sensor_4.TRIG
  N12: Rasberry_Pi_Pico_W.pin_20, HC-SR04_Sensor_4.ECHO
  N13: Rasberry_Pi_Pico_W.pin_24, DC_Mot_Enc2.pin3
  N14: Rasberry_Pi_Pico_W.pin_25, DC_Mot_Enc2.pin4
  N15: Rasberry_Pi_Pico_W.pin_26, DC_Mot_Enc1.pin3
  N16: Rasberry_Pi_Pico_W.pin_27, DC_Mot_Enc1.pin4
  VCC: Rasberry_Pi_Pico_W.pin_36, HC-SR04_Sensor_1.VCC, HC-SR04_Sensor_2.VCC, HC-SR04_Sensor_3.VCC, HC-SR04_Sensor_4.VCC, DC_Mot_Enc1.pin5, DC_Mot_Enc2.pin5
  N17: DC_Mot_Enc1.pin1, Cytron_MDD10A.no_name_yet#connectorM1A-1
  N18: DC_Mot_Enc1.pin6, Cytron_MDD10A.no_name_yet#connectorM1B-1
  N19: DC_Mot_Enc2.pin1, Cytron_MDD10A.no_name_yet#connectorM2A-1
  N20: DC_Mot_Enc2.pin6, Cytron_MDD10A.no_name_yet#connectorM2B-1
  N21: Bat1.+#0, Bat3.+#1
  N22: Bat1.+#1, Bat2.+#0
  N23: Bat2.+#1, Cytron_MDD10A.no_name_yet#connectorBatt-1
  N24: Bat3.+#0, Cytron_MDD10A.no_name_yet#connectorBatt-2
  5V: Mod1.5V, Part1.VCC
  GND_2: Mod1.GND, Part1.GND
  N25: Mod1.GPIO22, Part1.SDA/MISO/TX
  N26: Mod1.GPIO23, Part1.SCL/SCK/RX

notes:
  LEFT_MOTOR
  RIGHT_MOTOR

custom parts:
  Raspberry Pi Pico W: Raspberry Pi Pico W. Based around the RP2040 microcontroller the Pico W is a low cost microcontroller device bringing Raspberry Pi quality, cost, and easy of use to the microcontroller space. The areas marked KEEPOUT in pcb silkscreen should not have traces running through them to avoid shorts on a soldered in module!
  battery_holder_single_18650: single 18650 battery holder
